// Logisim project BFPU.circ as structural Verilog: 1 circuit, main circuit main
module main (
);

  wire and_4_out, cells, CLK, JMP, load, nor_1_out, nor_2_out, not_1_out, not_2_out, not_3_out, not_4_out,
       not_5_out, not_6_out, or_3_out, RST, SAVE, SRV;
  wire [1:0] nor_3_out, or_1_out;
  wire [2:0] rom_1_data;
  wire [3:0] H, L;
  wire [7:0] adder_1_out, adder_2_out, multiplexer_1_out, multiplexer_2_out, ram_1_dout, register_1_q,
       register_2_q, subtractor_1_out;
  wire [14:0] adder_3_out, multiplexer_3_out, register_3_q, subtractor_2_out;

  Adder adder_1 (.a(register_1_q), .b(8'h1), .out(adder_1_out));  // open: cin, cout
  ROM #(.dataWidth(3)) rom_1 (.addr(register_1_q), .data(rom_1_data));
  Multiplexer #(.select(2), .width(8)) multiplexer_1 (
    .in0(adder_1_out), .in1(register_2_q), .in2({8{1'b0}}), .in3({8{1'b0}}), .out(multiplexer_1_out),
    .sel({RST, JMP}));
  Register register_1 (.D(multiplexer_1_out), .en(1'b1), .clk(CLK), .Q(register_1_q));  // open: clr
  Clock clock_1 (.out(CLK));
  Button u_RST (.out(RST));
  Hex_Digit_Display hex_digit_display_1 (.value(H));  // open: dp
  Hex_Digit_Display hex_digit_display_2 (.value(L));  // open: dp
  Register register_2 (.D(register_1_q), .en(SAVE), .clk(CLK), .Q(register_2_q));  // open: clr
  not not_1 (not_1_out, rom_1_data[0]);
  and and_1 (SAVE, not_1_out, rom_1_data[1], rom_1_data[2]);
  and and_2 (JMP, SRV, rom_1_data[0], rom_1_data[1], rom_1_data[2]);
  not not_2 (not_2_out, rom_1_data[1]);
  and and_3 (load, rom_1_data[2], not_2_out, rom_1_data[0]);
  not not_3 (not_3_out, rom_1_data[2]);
  not not_4 (not_4_out, rom_1_data[0]);
  not not_5 (not_5_out, rom_1_data[2]);
  not not_6 (not_6_out, rom_1_data[1]);
  nor nor_1 (nor_1_out, rom_1_data[0], not_6_out, rom_1_data[2]);
  and and_4 (and_4_out, rom_1_data[0], rom_1_data[1], not_3_out);
  nor nor_2 (nor_2_out, rom_1_data[0], rom_1_data[1], not_5_out);
  nor nor_3 (nor_3_out[0], rom_1_data[0], rom_1_data[1], rom_1_data[2]);
  nor nor_4 (nor_3_out[1], not_4_out, rom_1_data[1], rom_1_data[2]);
  or or_1 (or_1_out[0], nor_1_out, nor_2_out);
  or or_2 (or_1_out[1], and_4_out, nor_2_out);
  Adder adder_2 (.a(ram_1_dout), .b(8'h1), .out(adder_2_out));  // open: cin, cout
  Subtractor subtractor_1 (.a(ram_1_dout), .b(8'h1), .out(subtractor_1_out));  // open: bin, bout
  or or_3 (or_3_out, nor_3_out[0], nor_3_out[1]);
  Adder #(.width(15)) adder_3 (.a(register_3_q), .b(15'h1), .out(adder_3_out));  // open: cin, cout
  Subtractor #(.width(15)) subtractor_2 (.a(register_3_q), .b(15'h1), .out(subtractor_2_out));  // open: bin, bout
  Multiplexer #(.select(2), .width(8)) multiplexer_2 (
    .in0(ram_1_dout), .in1(adder_2_out), .in2(subtractor_1_out), .in3(8'haa), .out(multiplexer_2_out),
    .sel(or_1_out));
  not not_7 (cells, or_3_out);
  Multiplexer #(.select(2), .width(15)) multiplexer_3 (
    .in0(register_3_q), .in1(adder_3_out), .in2(subtractor_2_out), .out(multiplexer_3_out), .sel(nor_3_out));  // open: in3
  RAM #(.addrWidth(15)) ram_1 (
    .addr(register_3_q), .we(cells), .oe(1'b1), .clk(CLK), .din(multiplexer_2_out), .dout(ram_1_dout));
  Register #(.width(15)) register_3 (.D(multiplexer_3_out), .en(1'b1), .clk(CLK), .Q(register_3_q));  // open: clr
  or or_4 (SRV, ram_1_dout[0], ram_1_dout[1], ram_1_dout[2], ram_1_dout[3], ram_1_dout[4], ram_1_dout[5], ram_1_dout[6], ram_1_dout[7]);
  Register register_4 (.D(ram_1_dout), .en(load), .clk(CLK), .Q({H, L}));  // open: clr

  // Notes on the sheet:
  //   contents of rom_1 (hex, n*v repeats v):
  //   2 3 2 6 5 3 7 25*0 6 15*0 7 15*0 7
  //   Programmspeicher
  //   Prozessorlogik
  //   Instruction Pointer
  //   I/O Anschlüsse
  //   Procssor clock
  //   RESET
  //   Eingabevektor
  //   Ausgabevektor
  //   Load address
  //   Branch
  //   Decoder
  //   . / set
  //   > / ptr++
  //   < / ptr--
  //   ALU
  //   + / cell[ptr]++
  //   - / cell[ptr]--
  //   pointer register
  //   Zellenblock
  //   Brainfuck Logik
endmodule
